// Logisim project labo_checksum_etu.circ as structural Verilog: 8 circuits, main circuit Add1bit
module Add1bit (
  input  a_i,
  input  b_i,
  input  c_i,
  output r_o,
  output c_o
);

  wire and_1_out, and_2_out, and_3_out, xor_1_out;

  xor xor_1 (xor_1_out, a_i, b_i);
  and and_1 (and_1_out, a_i, b_i);
  and and_2 (and_2_out, a_i, c_i);
  and and_3 (and_3_out, b_i, c_i);
  xor xor_2 (r_o, xor_1_out, c_i);
  or or_1 (c_o, and_1_out, and_2_out, and_3_out);

  // Notes on the sheet:
  //   Attention, votre version de Logisim
  //   ne contient pas de tracker. Si vous
  //   enregistrez votre projet, toutes les
  //   informations du tracker seront
  //   définitivement effacées.
endmodule

module Add4bit (
  input  c_i,
  input  [3:0] a_i,
  input  [3:0] b_i,
  output [3:0] r_o,
  output c_o
);

  wire add1bit_1_c_o, add1bit_2_c_o, add1bit_3_c_o;

  Add1bit add1bit_1 (.a_i(a_i[0]), .b_i(b_i[0]), .c_i(c_i), .r_o(r_o[0]), .c_o(add1bit_1_c_o));
  Add1bit add1bit_2 (.a_i(a_i[1]), .b_i(b_i[1]), .c_i(add1bit_1_c_o), .r_o(r_o[1]), .c_o(add1bit_2_c_o));
  Add1bit add1bit_3 (.a_i(a_i[2]), .b_i(b_i[2]), .c_i(add1bit_2_c_o), .r_o(r_o[2]), .c_o(add1bit_3_c_o));
  Add1bit add1bit_4 (.a_i(a_i[3]), .b_i(b_i[3]), .c_i(add1bit_3_c_o), .r_o(r_o[3]), .c_o(c_o));

  // Notes on the sheet:
  //   Attention, votre version de Logisim
  //   ne contient pas de tracker. Si vous
  //   enregistrez votre projet, toutes les
  //   informations du tracker seront
  //   définitivement effacées.
endmodule

module Sub4bit (
  input  [3:0] a_i,
  input  [3:0] b_i,
  output [3:0] r_o,
  output c_o
);

  wire add4bit_1_c_o;
  wire [3:0] not_1_out;

  assign not_1_out = ~b_i;  // NOT_Gate not_1, 4 bits wide
  Add4bit add4bit_1 (.c_i(1'b1), .a_i(a_i), .b_i(not_1_out), .r_o(r_o), .c_o(add4bit_1_c_o));
  xor xor_1 (c_o, 1'b1, add4bit_1_c_o);

  // Notes on the sheet:
  //   Attention, votre version de Logisim
  //   ne contient pas de tracker. Si vous
  //   enregistrez votre projet, toutes les
  //   informations du tracker seront
  //   définitivement effacées.
endmodule

module AddSub4bit (
  input  sel_i,
  input  [3:0] a_i,
  input  [3:0] b_i,
  output [3:0] r_o,
  output c_o
);

  wire add4bit_1_c_o;
  wire [3:0] xor_1_out;

  assign xor_1_out = {4{sel_i}} ^ b_i;  // XOR_Gate xor_1, 4 bits wide
  Add4bit add4bit_1 (.c_i(sel_i), .a_i(a_i), .b_i(xor_1_out), .r_o(r_o), .c_o(add4bit_1_c_o));
  xor xor_2 (c_o, sel_i, add4bit_1_c_o);

  // Notes on the sheet:
  //   Attention, votre version de Logisim
  //   ne contient pas de tracker. Si vous
  //   enregistrez votre projet, toutes les
  //   informations du tracker seront
  //   définitivement effacées.
endmodule

module Add8bit (
  input  c_i,
  input  [7:0] a_i,
  input  [7:0] b_i,
  output [7:0] r_o,
  output c_o
);

  wire add4bit_1_c_o;

  Add4bit add4bit_1 (.c_i(c_i), .a_i(a_i[3:0]), .b_i(b_i[3:0]), .r_o(r_o[3:0]), .c_o(add4bit_1_c_o));
  Add4bit add4bit_2 (.c_i(add4bit_1_c_o), .a_i(a_i[7:4]), .b_i(b_i[7:4]), .r_o(r_o[7:4]), .c_o(c_o));

  // Notes on the sheet:
  //   Attention, votre version de Logisim
  //   ne contient pas de tracker. Si vous
  //   enregistrez votre projet, toutes les
  //   informations du tracker seront
  //   définitivement effacées.
endmodule

module AddSub8bit (
  input  sel_i,
  input  [7:0] a_i,
  input  [7:0] b_i,
  output [7:0] r_o,
  output c_o
);

  wire add8bit_1_c_o;
  wire [7:0] xor_1_out;

  assign xor_1_out = {8{sel_i}} ^ b_i;  // XOR_Gate xor_1, 8 bits wide
  Add8bit add8bit_1 (.c_i(sel_i), .a_i(a_i), .b_i(xor_1_out), .r_o(r_o), .c_o(add8bit_1_c_o));
  xor xor_2 (c_o, sel_i, add8bit_1_c_o);

  // Notes on the sheet:
  //   Attention, votre version de Logisim
  //   ne contient pas de tracker. Si vous
  //   enregistrez votre projet, toutes les
  //   informations du tracker seront
  //   définitivement effacées.
endmodule

module Checksum (
  input  [7:0] a_i,
  input  [7:0] b_i,
  input  [7:0] c_i,
  output [7:0] r_o
);

  wire [7:0] add8bit_1_r_o, add8bit_2_r_o;

  Add8bit add8bit_1 (.c_i(1'b0), .a_i(a_i), .b_i(b_i), .r_o(add8bit_1_r_o));  // open: c_o
  Add8bit add8bit_2 (.c_i(1'b0), .a_i(add8bit_1_r_o), .b_i(c_i), .r_o(add8bit_2_r_o));  // open: c_o
  AddSub8bit addsub8bit_1 (.sel_i(1'b1), .a_i({8{1'b0}}), .b_i(add8bit_2_r_o), .r_o(r_o));  // open: c_o

  // Notes on the sheet:
  //   Attention, votre version de Logisim
  //   ne contient pas de tracker. Si vous
  //   enregistrez votre projet, toutes les
  //   informations du tracker seront
  //   définitivement effacées.
endmodule

module VerifyIntegrity (
  input  [7:0] a_i,
  input  [7:0] b_i,
  input  [7:0] c_i,
  input  [7:0] d_i,
  output verif_checksum_o
);


  // Notes on the sheet:
  //   Attention, votre version de Logisim
  //   ne contient pas de tracker. Si vous
  //   enregistrez votre projet, toutes les
  //   informations du tracker seront
  //   définitivement effacées.
endmodule
